// Logisim project sap1_g.circ as structural Verilog: 14 circuits, main circuit main
module main (
  input  Reset,
  output [3:0] high,
  output [3:0] low,
  output out_4,
  output out_5,
  output out_6,
  output out_7,
  output out_8,
  output out_9,
  output out_10,
  output out_11
);

  wire CLK, clock_1_out, controlador_sequencializador_1_hlt, Cp, Ea, El, Ep, Eu, La, nCE, nEi, nLa, nLb, nLi,
       nLm, nLo, not_1_out, not_2_out, not_3_out, not_4_out, \registrador_de_instruções_1_l4 ,
       \registrador_de_instruções_1_l5 , \registrador_de_instruções_1_l6 , \registrador_de_instruções_1_l7 ,
       Su;
  wire [3:0] rem_1_addr_out;
  wire [7:0] acumulador_1_a_dataout1, registrador_b_1_b_dataout;

  Clock clock_1 (.out(clock_1_out));
  assign CLK = not_1_out ? clock_1_out : 1'bz;  // Controlled_Buffer controlled_buffer_1
  not not_1 (not_1_out, controlador_sequencializador_1_hlt);
  not not_2 (not_2_out, CLK);
  Controlador_Sequencializador controlador_sequencializador_1 (
    .CLK(Reset), .CLR(CLK), .Ep(Ep), .Cp(Cp), .l7(\registrador_de_instruções_1_l7 ),
    .l6(\registrador_de_instruções_1_l6 ), .l5(\registrador_de_instruções_1_l5 ),
    .l4(\registrador_de_instruções_1_l4 ), .HLT(controlador_sequencializador_1_hlt), .nLm(nLm), .nCE(nCE),
    .EI(El), .La(La), .Ea(Ea), .Su(Su), .Eu(Eu), .nLb(nLb), .nLo(nLo), .nLi(nLi));
  CP cp_1 (.Ep(Ep), .nCLR(Reset), .nCLK(not_2_out), .CP_dataOut(low), .Cp(Cp));
  REM rem_1 (.ADDR_In(low), .nLm(nLm), .CLK(CLK), .ADDR_Out(rem_1_addr_out));
  not not_3 (not_3_out, nCE);
  \Registrador_de_Instruções  \registrador_de_instruções_1  (
    .out_6({high, low}), .in_1({high, low}), .l4(\registrador_de_instruções_1_l4 ),
    .l5(\registrador_de_instruções_1_l5 ), .l6(\registrador_de_instruções_1_l6 ),
    .l7(\registrador_de_instruções_1_l7 ), .nEi(nEi), .CLR(Reset), .Clk(CLK), .nLi(nLi));
  RAM #(.addrWidth(4)) ram_1 (
    .addr(rem_1_addr_out), .data({high, low}), .sel(not_3_out), .clk(CLK), .ld(not_3_out));  // open: clr
  Acumulador acumulador_1 (
    .A_dataIn({high, low}), .nLa(nLa), .CLK(CLK), .Ea(Ea), .A_dataOut1(acumulador_1_a_dataout1),
    .A_dataOut2({low, high}));
  Somador_Subtrator somador_subtrator_1 (
    .Su(Su), .B_data(registrador_b_1_b_dataout), .A_data(acumulador_1_a_dataout1), .Eu(Eu),
    .A_dataOut2({high, low}));
  Registrador_B registrador_b_1 (.B_dataIn({high, low}), .nLb(nLb), .CLK(CLK), .B_dataOut(registrador_b_1_b_dataout));
  not not_4 (not_4_out, nLo);
  Hex_Digit_Display hex_digit_display_1 (.value({out_4, out_5, out_6, out_7}));  // open: dp
  Register register_1 (
    .D({low, high}), .en(not_4_out), .Q({out_4, out_5, out_6, out_7, out_8, out_9, out_10, out_11}),
    .clk(CLK), .clr(Reset));
  Hex_Digit_Display hex_digit_display_2 (.value({out_8, out_9, out_10, out_11}));  // open: dp

  // Other names for the same wires on the sheet: CLR = Reset
endmodule

module CP (
  input  Cp,
  input  nCLK,
  input  nCLR,
  input  Ep,
  output [3:0] CP_dataOut
);

  wire not_1_out;
  wire [3:0] counter_1_q;

  not not_1 (not_1_out, nCLR);
  Counter #(.width(4), .max('hf), .trigger("falling")) counter_1 (
    .count(Cp), .Q(counter_1_q), .clk(nCLK), .clr(not_1_out));  // open: load, D, carry
  assign CP_dataOut = Ep ? counter_1_q : 4'bz;  // Controlled_Buffer controlled_buffer_1
endmodule

module Acumulador (
  input  [7:0] A_dataIn,
  input  nLa,
  input  CLK,
  input  Ea,
  output [7:0] A_dataOut1,
  output [7:0] A_dataOut2
);

  wire not_1_out;

  Register register_1 (.D(A_dataIn), .en(not_1_out), .Q(A_dataOut1), .clk(CLK));  // open: clr
  not not_1 (not_1_out, nLa);
  assign A_dataOut2 = Ea ? A_dataOut1 : 8'bz;  // Controlled_Buffer controlled_buffer_1
endmodule

module Somador_Subtrator (
  input  Su,
  input  [7:0] B_data,
  input  [7:0] A_data,
  input  Eu,
  output [7:0] A_dataOut2
);

  wire [7:0] adder_1_out, xor_1_out;

  assign xor_1_out = {8{Su}} ^ B_data;  // XOR_Gate xor_1, 8 bits wide
  Adder adder_1 (.a(xor_1_out), .b(A_data), .out(adder_1_out), .cin(Su));  // open: cout
  assign A_dataOut2 = Eu ? adder_1_out : 8'bz;  // Controlled_Buffer controlled_buffer_1
endmodule

module Registrador_B (
  input  [7:0] B_dataIn,
  input  nLb,
  input  CLK,
  output [7:0] B_dataOut
);

  wire not_1_out;

  Register register_1 (.D(B_dataIn), .en(not_1_out), .Q(B_dataOut), .clk(CLK));  // open: clr
  not not_1 (not_1_out, nLb);
endmodule

module \Memória_RAM  (
  input  [3:0] MEM_ADDR,
  input  [7:0] MEM_dataIn,
  input  PROG,
  input  nEscrita_Leitura,
  input  nCE,
  output [7:0] MEM_dataOut
);

  wire not_1_out, not_2_out;
  wire [7:0] controlled_buffer_1_out, ram_1_data;

  RAM #(.addrWidth(4)) ram_1 (
    .addr(MEM_ADDR), .data(ram_1_data), .sel(1'b1), .clk(PROG), .ld(nEscrita_Leitura));  // open: clr
  not not_1 (not_1_out, nCE);
  assign controlled_buffer_1_out = nEscrita_Leitura ? ram_1_data : 8'bz;  // Controlled_Buffer controlled_buffer_1
  not not_2 (not_2_out, nEscrita_Leitura);
  assign ram_1_data = not_2_out ? MEM_dataIn : 8'bz;  // Controlled_Buffer controlled_buffer_2
  assign MEM_dataOut = not_1_out ? controlled_buffer_1_out : 8'bz;  // Controlled_Buffer controlled_buffer_3
endmodule

module REM (
  input  [3:0] ADDR_In,
  input  nLm,
  input  CLK,
  output [3:0] ADDR_Out
);

  wire not_1_out;

  Register #(.width(4)) register_1 (.D(ADDR_In), .en(not_1_out), .Q(ADDR_Out), .clk(CLK));  // open: clr
  not not_1 (not_1_out, nLm);
endmodule

module \Registrador_de_Instruções  (
  input  [7:0] in_1,
  input  nLi,
  input  Clk,
  input  CLR,
  input  nEi,
  output [7:0] out_6,
  output l4,
  output l5,
  output l6,
  output l7
);

  wire not_1_out, not_2_out;
  wire [3:0] register_1_q;
  wire [7:0] bit_extender_1_out, controlled_buffer_1_out;

  not not_1 (not_1_out, nLi);
  Register register_1 (.D(in_1), .en(not_1_out), .Q({l7, l6, l5, l4, register_1_q}), .clk(Clk), .clr(CLR));
  not not_2 (not_2_out, nEi);
  assign bit_extender_1_out = {{4{1'b0}}, register_1_q};  // Bit_Extender bit_extender_1
  assign controlled_buffer_1_out = not_2_out ? bit_extender_1_out : 8'bz;  // Controlled_Buffer controlled_buffer_1
endmodule

module Controlador_Sequencializador (
  input  CLK,
  input  CLR,
  input  l7,
  input  l5,
  input  l6,
  input  l4,
  output Ep,
  output Cp,
  output HLT,
  output nLm,
  output nCE,
  output EI,
  output La,
  output Ea,
  output Eu,
  output nLb,
  output nLo,
  output nLi,
  output Su
);

  wire c39_1_out_7, c39_1_out_8, c39_1_out_9, c39_1_out_10, c40_1_out_7, c40_1_out_8, c40_1_out_9,
       c40_1_out_10, c41_1_out_8, c41_1_out_9, c41_1_out_10, c41_1_out_11, c41_2_out_10, c41_2_out_11,
       c43_1_out_6, c43_1_out_7, c43_1_out_8, idecoder_1_add, idecoder_1_lda, idecoder_1_out, idecoder_1_sub,
       nor_1_out, not_1_out, or_1_out, or_2_out, or_3_out, or_4_out, or_6_out, shift_register_1_q2,
       shift_register_1_q3, shift_register_1_q4, shift_register_1_q5;

  iDecoder idecoder_1 (
    .l7(l7), .l6(l6), .l5(l5), .l4(l4), .LDA(idecoder_1_lda), .ADD(idecoder_1_add), .SUB(idecoder_1_sub),
    .OUT(idecoder_1_out), .HLT(HLT));
  C39 c39_1 (
    ._1(idecoder_1_lda), ._4(idecoder_1_add), ._9(idecoder_1_sub), ._10(shift_register_1_q3),
    ._12(idecoder_1_lda), ._13(shift_register_1_q4), .out_7(c39_1_out_7), .out_8(c39_1_out_8),
    .out_9(c39_1_out_9), .out_10(c39_1_out_10));
  not not_1 (not_1_out, CLK);
  C40 c40_1 (
    ._1(idecoder_1_add), ._4(idecoder_1_sub), ._5(shift_register_1_q4), ._9(idecoder_1_lda),
    ._12(idecoder_1_add), ._13(shift_register_1_q3), .out_7(c40_1_out_7), .out_8(c40_1_out_8),
    .out_9(c40_1_out_9), .out_10(c40_1_out_10));
  or or_1 (or_1_out, Ep, c39_1_out_7, c39_1_out_8, c39_1_out_9);
  or or_2 (or_2_out, shift_register_1_q2, c39_1_out_10, c40_1_out_7, c40_1_out_8);
  not not_2 (nCE, or_2_out);
  not not_3 (nLm, or_1_out);
  Shift_Register #(.length(6)) shift_register_1 (
    .in(nor_1_out), .clk(not_1_out), .clr(CLR), .q0(Ep), .q1(Cp), .q2(shift_register_1_q2),
    .q3(shift_register_1_q3), .q4(shift_register_1_q4), .q5(shift_register_1_q5));  // open: shift, out, load, d0, d1, d2, d3, d4, d5
  C41 c41_1 (
    ._1(idecoder_1_sub), ._2(shift_register_1_q3), ._4(idecoder_1_lda), ._5(shift_register_1_q4),
    ._9(idecoder_1_add), ._12(idecoder_1_sub), ._13(shift_register_1_q5), .out_8(c41_1_out_8),
    .out_9(c41_1_out_9), .out_10(c41_1_out_10), .out_11(c41_1_out_11));
  or or_3 (or_3_out, c40_1_out_9, c40_1_out_10, c41_1_out_8);
  or or_4 (or_4_out, c41_1_out_9, c41_1_out_10, c41_1_out_11);
  not not_4 (La, or_4_out);
  not not_5 (EI, or_3_out);
  C41 c41_2 (
    ._1(idecoder_1_out), ._2(shift_register_1_q3), ._4(idecoder_1_sub), ._5(shift_register_1_q5),
    ._9(idecoder_1_add), ._12(idecoder_1_sub), ._13(shift_register_1_q5), .out_8(Ea), .out_9(Su),
    .out_10(c41_2_out_10), .out_11(c41_2_out_11));
  or or_5 (Eu, c41_2_out_10, c41_2_out_11);
  C43 c43_1 (
    ._1(idecoder_1_add), ._4(idecoder_1_sub), ._5(shift_register_1_q4), ._9(idecoder_1_out),
    ._10(shift_register_1_q3), .out_6(c43_1_out_6), .out_7(c43_1_out_7), .out_8(c43_1_out_8));
  or or_6 (or_6_out, c43_1_out_6, c43_1_out_7);
  not not_6 (nLb, or_6_out);
  nor nor_1 (nor_1_out, Ep, Cp, shift_register_1_q2, shift_register_1_q3, shift_register_1_q4);
  not not_7 (nLo, c43_1_out_8);
  not not_8 (nLi, shift_register_1_q2);
endmodule

module C39 (
  input  _1,
  input  _4,
  input  _9,
  input  _10,
  input  _13,
  input  _12,
  output out_7,
  output out_8,
  output out_9,
  output out_10
);

  and and_1 (out_7, _1, _10);
  and and_2 (out_8, _4, _10);
  and and_3 (out_9, _9, _10);
  and and_4 (out_10, _12, _13);
endmodule

module C40 (
  input  _1,
  input  _4,
  input  _5,
  input  _9,
  input  _12,
  input  _13,
  output out_7,
  output out_8,
  output out_9,
  output out_10
);

  and and_1 (out_7, _1, _5);
  and and_2 (out_8, _4, _5);
  and and_3 (out_9, _9, _13);
  and and_4 (out_10, _12, _13);
endmodule

module C41 (
  input  _4,
  input  _5,
  input  _9,
  input  _12,
  input  _13,
  input  _1,
  input  _2,
  output out_8,
  output out_9,
  output out_10,
  output out_11
);

  and and_1 (out_8, _1, _2);
  and and_2 (out_9, _4, _5);
  and and_3 (out_10, _9, _13);
  and and_4 (out_11, _12, _13);
endmodule

module C43 (
  input  _4,
  input  _5,
  input  _1,
  input  _9,
  input  _10,
  output out_6,
  output out_7,
  output out_8
);

  and and_1 (out_6, _1, _5);
  and and_2 (out_7, _4, _5);
  and and_3 (out_8, _9, _10);
endmodule

module iDecoder (
  input  l7,
  input  l6,
  input  l5,
  input  l4,
  output LDA,
  output ADD,
  output SUB,
  output OUT,
  output HLT
);

  wire and_1_out, and_2_out, and_3_out, and_4_out, and_5_out, not_1_out, not_2_out, not_3_out, not_4_out;

  not not_1 (not_1_out, l7);
  not not_2 (not_2_out, l6);
  not not_3 (not_3_out, l5);
  not not_4 (not_4_out, l4);
  and and_1 (and_1_out, not_1_out, not_2_out, not_3_out, not_4_out);
  and and_2 (and_2_out, not_1_out, not_2_out, not_3_out, l4);
  and and_3 (and_3_out, not_1_out, not_2_out, l5, not_4_out);
  and and_4 (and_4_out, l7, l6, l5, not_4_out);
  and and_5 (and_5_out, l7, l6, l5, l4);
  buf buffer_1 (LDA, and_1_out);
  buf buffer_2 (ADD, and_2_out);
  buf buffer_3 (SUB, and_3_out);
  buf buffer_4 (OUT, and_4_out);
  buf buffer_5 (HLT, and_5_out);
endmodule
